# Fritzing sketch lcd1602 (saved by Fritzing 0.9.3b)

parts:
  WeMos_D1_Mini1 = WeMos D1 Mini
  LCM1602_IIC1 = LCM1602 IIC [part_number="LCM1602 IIC" chip_label="LCM1602 IIC" package="DIP (Dual Inline) [THT]"]
  U1 = LCD-16X2 [package=lcd-16x2_noholes]

nets:
  3V3: WeMos_D1_Mini1.3V3, LCM1602_IIC1.VCC
  N1: WeMos_D1_Mini1.D1, LCM1602_IIC1.SCL
  N2: WeMos_D1_Mini1.D2, LCM1602_IIC1.SDA
  N3: WeMos_D1_Mini1.G, LCM1602_IIC1.GND
  VSS: LCM1602_IIC1.VSS, U1.VSS
  VDD: LCM1602_IIC1.VDD, U1.VDD
  N4: LCM1602_IIC1.V0, U1.VO
  N5: LCM1602_IIC1.RS, U1.RS
  N6: LCM1602_IIC1.RW, U1.R_W
  N7: LCM1602_IIC1.E, U1.E
  N8: LCM1602_IIC1.D0, U1.DB0
  N9: LCM1602_IIC1.D1, U1.DB1
  N10: LCM1602_IIC1.D2, U1.DB2
  N11: LCM1602_IIC1.D3, U1.DB3
  N12: LCM1602_IIC1.D4, U1.DB4
  N13: LCM1602_IIC1.D5, U1.DB5
  N14: LCM1602_IIC1.D6, U1.DB6
  N15: LCM1602_IIC1.D7, U1.DB7
  N16: LCM1602_IIC1.A, U1.A
  N17: LCM1602_IIC1.K, U1.K
  N18: LCM1602_IIC1.LED_A, LCM1602_IIC1.LED_B

notes:
  [It's possible to power LCD from 5V]

custom parts:
  LCM1602 IIC: I2C-Module to use a 1602 or 2004 LCD on with the wire.h libory Serial LCD Modul
