# Fritzing sketch weather_station (saved by Fritzing 0.9.3b)
breadboards: 1

parts:
  WeMos_D1_Mini1 = WeMos D1 Mini
  RHT1 = Humidity and Temperature Sensor RHT03
  R1 = Resistor [tolerance=±5% resistance=4.7k package="0402 [SMD]"]
  Part1 = Adafruit CCS811 [part_number="Adafruit #3566"]
  R2 = Resistor [tolerance=±5% resistance=3k package=THT]
  J1 = Piezo Speaker
  D2 = Rectifier Diode [part_number=1N4001 package="300 mil [THT]"]
  Q2 = NPN-Transistor [part_number=PN2222 package="TO92 [THT]"]

nets:
  3V3: WeMos_D1_Mini1.3V3, Part1.3.3V
  5V: WeMos_D1_Mini1.5V, RHT1.Vcc, R1.Pin_1
  N1: WeMos_D1_Mini1.D0, RHT1.Data-signal
  N2: WeMos_D1_Mini1.D1, Part1.SCL
  N3: WeMos_D1_Mini1.D2, Part1.SDA
  N4: WeMos_D1_Mini1.D5, R2.Pin_0
  N5: WeMos_D1_Mini1.G, RHT1.GND_2, Part1.GND, Part1.!WAKE, Q2.E
  N6: R2.Pin_1, Q2.B
  N7: J1.pin1, D2.anode, Q2.C
  N8: J1.pin2, D2.cathode

custom parts:
  Adafruit CCS811: Breathe easy - we finally have an I2C VOC/eCO2 sensor in the Adafruit shop! Add air quality monitoring to your project and with an Adafruit CCS811 Air Quality Sensor Breakout. This sensor from AMS is a gas sensor that can detect a wide range of Volatile Organic Compounds (VOCs) and is intended for indoor air quality monitoring. When connected to your microcontroller (running our library code)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
